# Fritzing sketch LA_scheme (saved by Fritzing 0.9.3b)
stripboards: 2

parts:
  Mod1 = Raspberry Pi 4B
  M1 = linear actuator [package=THT]
  BAT1 = 12 battery [package=battery]
  DPDT_Relay1 = DPDT Relay [chip_label=Relay package="DIP (Dual Inline) [THT]"]
  D1 = Rectifier Diode 10A [part_number=P1000K]
  R1 = Resistor [tolerance=±5% resistance=680 power=0pW package="2512 [SMD]"]
  Q1 = NPN-Transistor [package="TO92 [THT]"]

nets:
  N1: Mod1.GPIO21, R1.Pin_0
  N2: M1.pin1, DPDT_Relay1.pin6
  N3: M1.pin2, DPDT_Relay1.pin3
  N4: BAT1.-, DPDT_Relay1.pin4, Q1.B
  N5: BAT1.+, DPDT_Relay1.pin5
  N6: DPDT_Relay1.pin1, D1.anode, Q1.E
  N7: DPDT_Relay1.pin8, D1.cathode
  N8: R1.Pin_1, Q1.C

custom parts:
  linear actuator: Generic linear actuator.
  12 battery: 12V lead acid type battery, like the Husqvarna YTH2448 12V 35AH battery. This is the mini version 1/4 the size of the actual battery to be closer to typical breadboard parts (around 2in wide rathher than 7in). The pads in pcb are sized to accomidate up to 14ga wire (as these batterys will deliver high currents.)
  DPDT Relay: DIP DPDT Relay (Double Pole Double Throw)
