# Fritzing sketch LA_scheme_2 (saved by Fritzing 0.9.3b)

parts:
  Mod1 = Raspberry Pi 4B
  M1 = linear actuator [package=THT]  # not connected
  BAT1 = 12 battery [package=battery]  # not connected

nets:
  N1: Mod1.GPIO4, Mod1.GPIO14
  N2: Mod1.GND, Mod1.GPIO21

custom parts:
  linear actuator: Generic linear actuator.
  12 battery: 12V lead acid type battery, like the Husqvarna YTH2448 12V 35AH battery. This is the mini version 1/4 the size of the actual battery to be closer to typical breadboard parts (around 2in wide rathher than 7in). The pads in pcb are sized to accomidate up to 14ga wire (as these batterys will deliver high currents.)
